// Logisim project CPU 8 BITS.circ as structural Verilog: 3 circuits, main circuit CPU
module CPU (
  input  [7:0] in_1,
  input  [7:0] in_2,
  input  [7:0] in_3,
  input  [7:0] in_4,
  input  [7:0] in_5,
  input  [7:0] in_6,
  input  [7:0] in_7,
  output [7:0] out_8,
  output [7:0] out_9,
  output [7:0] out_10
);

  wire ADD_Rx__Ry, Clock, controlled_buffer_6_out, HLT, MOV_Rx__Ra, MOV_Rx__Ry, not_1_out, RDM_Rx__End,
       STR_End__Rx;
  wire [1:0] controlled_buffer_3_out, controlled_buffer_9_out;
  wire [4:0] counter_1_q;
  wire [7:0] adder_1_out, controlled_buffer_1_out, controlled_buffer_2_out, controlled_buffer_5_out,
       controlled_buffer_7_out, RX_end, VALOR_1, VALOR_2;

  DotMatrix #(.matrixcols(15), .matrixrows(8)) dotmatrix_1 (
    .col1(in_1), .col2(in_4), .col3(in_4), .col5(in_2), .col6(in_5), .col7(in_5), .col8(in_7), .col10(in_3),
    .col11(in_6), .col12(in_6), .col13(in_3));  // open: col0, col4, col9, col14
  Decoder #(.select(4), .enable("false")) decoder_1 (
    .out8(HLT), .out9(ADD_Rx__Ry), .out11(MOV_Rx__Ry), .out12(MOV_Rx__Ra), .out13(RDM_Rx__End),
    .out14(STR_End__Rx), .sel(out_8[7:4]));  // open: out0, out1, out2, out3, out4, out5, out6, out7, out10, out15
  Clock clock_1 (.out(Clock));
  assign controlled_buffer_1_out = ADD_Rx__Ry ? VALOR_1 : 8'bz;  // Controlled_Buffer controlled_buffer_1
  assign controlled_buffer_2_out = ADD_Rx__Ry ? VALOR_2 : 8'bz;  // Controlled_Buffer controlled_buffer_2
  assign controlled_buffer_3_out = RDM_Rx__End ? out_8[1:0] : 2'bz;  // Controlled_Buffer controlled_buffer_3
  Adder adder_1 (.a(controlled_buffer_1_out), .b(controlled_buffer_2_out), .out(adder_1_out));  // open: cin, cout
  Register #(.trigger("falling")) RA (.D(adder_1_out), .Q(out_9), .clk(Clock));  // open: en, clr
  assign controlled_buffer_3_out = STR_End__Rx ? out_8[3:2] : 2'bz;  // Controlled_Buffer controlled_buffer_4
  assign controlled_buffer_5_out = STR_End__Rx ? RX_end : 8'bz;  // Controlled_Buffer controlled_buffer_5
  Counter #(.width(5), .max('h1e)) counter_1 (
    .Q(counter_1_q), .clk(controlled_buffer_6_out));  // open: load, D, count, carry, clr
  assign controlled_buffer_6_out = not_1_out ? Clock : 1'bz;  // Controlled_Buffer controlled_buffer_6
  not not_1 (not_1_out, HLT);
  RAM #(.addrWidth(2), .bus("separate")) ram_1 (
    .addr(controlled_buffer_3_out), .din(controlled_buffer_5_out), .data(out_10), .str(STR_End__Rx),
    .clk(Clock), .ld(RDM_Rx__End));  // open: sel, clr
  ROM #(.addrWidth(5)) rom_1 (.addr(counter_1_q), .data(out_8));  // open: sel
  assign controlled_buffer_7_out = RDM_Rx__End ? out_10 : 8'bz;  // Controlled_Buffer controlled_buffer_7
  assign controlled_buffer_7_out = MOV_Rx__Ra ? out_9 : 8'bz;  // Controlled_Buffer controlled_buffer_8
  assign controlled_buffer_9_out = MOV_Rx__Ra ? out_8[1:0] : 2'bz;  // Controlled_Buffer controlled_buffer_9
  assign controlled_buffer_9_out = RDM_Rx__End ? out_8[1:0] : 2'bz;  // Controlled_Buffer controlled_buffer_10
  Banco_de_Registradores banco_de_registradores_1 (
    .imput(controlled_buffer_7_out), .Select_Regist(controlled_buffer_9_out), .output2(VALOR_1),
    .output1(VALOR_2), .Select_OutReg(out_8[3:2]), .Select_outReg_2(out_8[1:0]), .in_3(Clock));  // open: CLER
  assign RX_end = STR_End__Rx ? VALOR_1 : 8'bz;  // Controlled_Buffer controlled_buffer_11

  // Other names for the same wires on the sheet: ACUMULADOR[7:0] = out_9; C0[7:0] = in_1; C1[7:0] = in_4;
  //   ID_RAM_Registrador_Y[1:0] = out_8[1:0]; ID_Registrador_X[1:0] = out_8[3:2]; ID_Instrução[3:0] = out_8[7:4];
  //   P0[7:0] = in_2; P1[7:0] = in_5; P3[7:0] = in_7; RAM_Output[7:0] = out_10; U0[7:0] = in_3; U1[7:0] = in_6

  // Notes on the sheet:
  //   Instruções
  //   Mnemônico   Hexa    Binário
  //   HLT                  0x8       1000
  //   ADD Rx, Ry      0x9       1001
  //   MOV Rx, Ry     0xB       1011
  //   MOV Rx, Ra     0xC       1100
  //   RDM Rx, End     0xD      1101
  //   STR End, Rx     0xE      1110
  //   Memória RAM
  //   Memória ROM
  //   contents of rom_1 (hex, n*v repeats v):
  //   d0 d5 91 c5 d2 d3 9e c0 91 c2 e2 80
endmodule

module Banco_de_Registradores (
  input  [7:0] imput,
  input  [1:0] Select_Regist,
  input  in_3,
  input  [1:0] Select_OutReg,
  input  [1:0] Select_outReg_2,
  output CLER,
  output [7:0] output2,
  output [7:0] output1
);

  wire Enable_R0, Enable_R1, Enable_R2, Enable_R3;
  wire [7:0] Output0, Output1_t, Output2_t, Output3;

  Decoder #(.select(2)) decoder_1 (
    .out0(Enable_R0), .out1(Enable_R1), .out2(Enable_R2), .out3(Enable_R3), .sel(Select_Regist), .en(in_3));
  Register #(.trigger("high")) R0 (.D(imput), .Q(Output0), .clk(Enable_R0), .clr(CLER));  // open: en
  Register #(.trigger("high")) R1 (.D(imput), .Q(Output1_t), .clk(Enable_R1), .clr(CLER));  // open: en
  Multiplexer #(.select(2), .width(8), .enable("false")) multiplexer_1 (
    .in0(Output0), .in1(Output1_t), .in2(Output2_t), .in3(Output3), .out(output1), .sel(Select_OutReg));
  Register #(.trigger("high")) R2 (.D(imput), .Q(Output2_t), .clk(Enable_R2), .clr(CLER));  // open: en
  Register #(.trigger("high")) R3 (.D(imput), .Q(Output3), .clk(Enable_R3), .clr(CLER));  // open: en
  Multiplexer #(.select(2), .width(8), .enable("false")) multiplexer_2 (
    .in0(Output0), .in1(Output1_t), .in2(Output2_t), .in3(Output3), .out(output2), .sel(Select_outReg_2));

  // Other names for the same wires on the sheet: Input[7:0] = imput
endmodule

module \Decodificador_de_Instruções  (
  input  [7:0] in_1
);

  wire ADD_Rx__Ry, HLT, MOV_Rx__Ra, MOV_Rx__Ry, RDM_Rx__End, STR_End__Rx;

  Decoder #(.select(4), .enable("false")) decoder_1 (
    .out8(HLT), .out9(ADD_Rx__Ry), .out11(MOV_Rx__Ry), .out12(MOV_Rx__Ra), .out13(RDM_Rx__End),
    .out14(STR_End__Rx), .sel(in_1[7:4]));  // open: out0, out1, out2, out3, out4, out5, out6, out7, out10, out15

  // Notes on the sheet:
  //   Instruções
  //   Mnemônico   Hexa    Binário
  //   HLT                  0x8       1000
  //   ADD Rx, Ry      0x9       1001
  //   MOV Rx, Ry     0xB       1011
  //   MOV Rx, Ra     0xC       1100
  //   RDM Rx, End     0xD      1101
  //   STR End, Rx     0xE      1110
endmodule
